# Fritzing sketch sat_fritzing (saved by Fritzing 1.0.1rc)
breadboards: 1

parts:
  Argon1 = Particle Argon
  A1 = u-blox NEO-6M GPS Breakout
  U1 = LIPO-1000mAh [package=lipo-1000]  # not connected
  J1 = Piezo Speaker

nets:
  N1: Argon1.GND, A1.Pin_2, J1.pin1
  N2: Argon1.RX, A1.Pin_3
  N3: Argon1.TX, A1.Pin_4
  N4: Argon1.D2, J1.pin2
  N5: Argon1.LI+, A1.Pin_1

custom parts:
  Particle Argon: The Argon is a powerful Wi-Fi enabled development board that can act as either a standalone Wi-Fi endpoint or Wi-Fi enabled gateway for Particle Mesh networks. It is based on the Nordic nRF52840 and has built-in battery charging circuitry so it’s easy to connect a Li-Po and deploy your local network in minutes. The Argon is great for connecting existing projects to the Particle Device Cloud or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
